# Fritzing sketch AD9851 (saved by Fritzing 0.9.6b)

parts:
  AD1 = DDS AD9850
  J1 = female pin header, 6 pins [form="♀ (female)"]
  R1 = Resistor [tolerance=±5% resistance=330 package="0603 [SMD]"]
  C1 = Ceramic Capacitor [capacitance=100nF voltage=35V package="0603 [SMD, multilayer]"]
  R3 = Resistor [tolerance=±1% resistance=0 part_number="3.9 KOhm" package="0603 [SMD]"]
  OMRON1 = OMRON PCB Power Relay – G5LE [part_number="G5LE-1\n" package=THT]  # not connected

nets:
  N1: AD1.GND, J1.pin1, C1.1
  N2: AD1.CLK, J1.pin4
  N3: AD1.FQ, J1.pin3
  N4: AD1.DATA, J1.pin2
  N5: J1.pin5, R1.Pin_0
  N6: R1.Pin_1, C1.0, R3.Pin_0

notes:
  Zynq-7010
  GND
  SD
  FQ_UD
  CK
  PWM
  TX
  +5Vcc
  to AD9851 pin 12 RSET
  RF out
  1 Vpp

custom parts:
  DDS AD9850: AD9850 DDS Signal Generator Module, frequency range 0 to 40MHz, sine or square wave output, on board 70MHz low pass filter, and 125MHz clock module. https://code.google.com/p/ad9850-arduino/
