# Fritzing sketch I2S (saved by Fritzing 0.9.4)
circuit board: 20.2231cm x 11.6432cm

parts:
  PCM5102A_I2S_Stereo_DAC1 = PCM5102A I2S Stereo DAC [part_number=PCM5102]
  M1 = PAM8403 Stereo Amplifier [part_number=PAM8403]
  SP1 = SPEAKER [package=pcb_mount_speaker]
  SP2 = SPEAKER [package=pcb_mount_speaker]
  R1 = Resistor [tolerance=±5% resistance=10k package=THT]
  U1 = V_REG_LD1117VXX [part_number="LM1117 5 to 3.3V" package=78xxl]
  J2 = female pin header, 2 pins [form="♀ (female)" part_number="+5V GND"]
  part = single row smd female pin header, 4 pins [form="♀ (female)" part_number="SCLK I2SDATA LRCLK GND"]
  part_2 = Capacitor [part_number="1 uF" package=cap-pth-small-kit]
  C2 = Capacitor [part_number="1 uF" package=cap-pth-small-kit]

nets:
  N1: PCM5102A_I2S_Stereo_DAC1.AGND#5, PCM5102A_I2S_Stereo_DAC1.ROUT, M1.INPUTR
  N2: PCM5102A_I2S_Stereo_DAC1.AGND#7, M1.INPUTG
  N3: PCM5102A_I2S_Stereo_DAC1.LROUT, M1.INPUTL
  N4: PCM5102A_I2S_Stereo_DAC1.SCK, R1.Pin_1
  N5: PCM5102A_I2S_Stereo_DAC1.BCK, part.pin1
  N6: PCM5102A_I2S_Stereo_DAC1.DIN, part.pin2
  N7: PCM5102A_I2S_Stereo_DAC1.LRCK, part.pin3
  GND: PCM5102A_I2S_Stereo_DAC1.GND, M1.POWER-, U1.GND, J2.pin2, part.pin4, part_2.2, C2.2
  N8: PCM5102A_I2S_Stereo_DAC1.VIN, R1.Pin_0, U1.OUT, C2.1
  N9: M1.ROUT-, SP1.+
  N10: M1.ROUT+, SP1.-
  N11: M1.LOUT+, SP2.-
  N12: M1.LOUT-, SP2.+
  N13: M1.POWER+, U1.IN, J2.pin1, part_2.1

notes:
  ZYNQ I2S EBAZ
  E19 I2SDATA DATA1_18
  F19 LRCLK DATA1_19
  K17 SCLK DATA1_20
  See also EBAZ.xdc (constraints)

custom parts:
  PAM8403 Stereo Amplifier: PAM8403 stereo amplifier module Descriptive words Links: PAM8403 product datasheet
